// Logisim project main.circ as structural Verilog: 17 circuits, main circuit main
// ~La
module main (
  input  [3:0] in_1,
  input  Clear,
  output [3:0] out_3,
  output [3:0] out_4,
  output HLT,
  output CP,
  output EP,
  output nLM,
  output nCE,
  output nLi,
  output nEi,
  output nLa,
  output EA,
  output SU,
  output EU,
  output nLb,
  output nLo
);

  wire clock_1_out, controlled_buffer_2_out, not_1_out, not_2_out, not_3_out, not_4_out, not_5_out,
       not_6_out, not_7_out, not_8_out, not_9_out;
  wire [3:0] accumulator_1_out, accumulator_1_out_2, ir_1_output0_3, ir_1_output4_7, mar_1_output;
  wire [7:0] b_register_1_out, output_register_1_out, transfer_1_to_adder_subtractor;

  not not_1 (not_1_out, controlled_buffer_2_out);
  not not_2 (not_2_out, nLM);
  not not_3 (not_3_out, nCE);
  not not_4 (not_4_out, nLi);
  ProgramCounter programcounter_1 (.Output(out_4), .Cp(CP), .CLK(not_1_out), .CLR(Clear), .Ep(EP));
  MAR mar_1 (.INPUT(out_4), .LOAD(not_2_out), .CLK(controlled_buffer_2_out), .CLR(Clear), .OUTPUT(mar_1_output));
  IR ir_1 (
    .LOAD(not_4_out), .CLK(controlled_buffer_2_out), .INPUT({out_3, out_4}), .OUTPUT4_7(ir_1_output4_7),
    .OUTPUT0_3(ir_1_output0_3), .ENABLE(1'b1), .CLR(Clear));
  RAM #(.addrWidth(4)) ram_1 (.addr(mar_1_output), .data({out_3, out_4}), .ld(not_3_out));  // open: sel, clk, clr
  assign out_4 = not_5_out ? ir_1_output0_3 : 4'bz;  // Controlled_Buffer controlled_buffer_1
  not not_5 (not_5_out, nEi);
  ControlSequencer controlsequencer_1 (
    .CLR(Clear), .I7_I4(ir_1_output4_7), .HLT(HLT), .CP(CP), .EP(EP), .LMbar(nLM), .CEbar(nCE), .LIbar(nLi),
    .EIbar(nEi), .LAbar(nLa), .EA(EA), .SU(SU), .EU(EU), .LBbar(nLb), .LObar(nLo),
    .CLK(controlled_buffer_2_out));
  Clock clock_1 (.out(clock_1_out));
  assign controlled_buffer_2_out = not_6_out ? clock_1_out : 1'bz;  // Controlled_Buffer controlled_buffer_2
  not not_6 (not_6_out, HLT);
  assign {out_3, out_4} = EA ? {accumulator_1_out_2, accumulator_1_out} : 8'bz;  // Controlled_Buffer controlled_buffer_3
  transfer transfer_1 (.in_1(SU), .from_B_reg(b_register_1_out), .To_adder_subtractor(transfer_1_to_adder_subtractor));
  Accumulator accumulator_1 (
    .nLa(not_7_out), .Clk(controlled_buffer_2_out), .Out({accumulator_1_out_2, accumulator_1_out}),
    .\input ({out_3, out_4}));
  not not_7 (not_7_out, nLa);
  Adder_Subtractor adder_subtractor_1 (
    .A({accumulator_1_out_2, accumulator_1_out}), .B(transfer_1_to_adder_subtractor), .Cin(SU),
    .Out({out_3, out_4}), .EU(EU));  // open: Cout
  B_register b_register_1 (
    .nlb(not_8_out), .Clk(controlled_buffer_2_out), .Out(b_register_1_out), .\input ({out_3, out_4}));
  not not_8 (not_8_out, nLb);
  output_register output_register_1 (
    .nlo(not_9_out), .Clk(controlled_buffer_2_out), .Out(output_register_1_out), .\input ({out_3, out_4}));
  Hex_Digit_Display hex_digit_display_1 (.value(accumulator_1_out_2));  // open: dp
  Hex_Digit_Display hex_digit_display_2 (.value(accumulator_1_out));  // open: dp
  not not_9 (not_9_out, nLo);
  Hex_Digit_Display hex_digit_display_3 (.value(output_register_1_out[7:4]));  // open: dp
  Hex_Digit_Display hex_digit_display_4 (.value(b_register_1_out[7:4]));  // open: dp
  Hex_Digit_Display hex_digit_display_5 (.value(b_register_1_out[3:0]));  // open: dp
  Hex_Digit_Display hex_digit_display_6 (.value(output_register_1_out[3:0]));  // open: dp

  // Notes on the sheet:
  //   1607091 and 1607115
  //   A reg
  //   B reg
  //   OUTPUT
  //   Operation: 9+11-8
endmodule

module MAR (
  input  LOAD,
  input  CLK,
  input  CLR,
  input  [3:0] INPUT,
  output [3:0] OUTPUT
);

  _4_bit_reg u_4_bit_reg_1 (
    .x3(INPUT[3]), .x2(INPUT[2]), .x1(INPUT[1]), .x0(INPUT[0]), .Load(LOAD), .CLK(CLK), .CL(CLR), .EN(1'b1),
    .y3(OUTPUT[3]), .y2(OUTPUT[2]), .y1(OUTPUT[1]), .y0(OUTPUT[0]));

  // Notes on the sheet:
  //   1607091
endmodule

// 8 bit Reg
module _8_bit_reg (
  input  Load,
  input  x7,
  input  x6,
  input  x5,
  input  x4,
  input  x3,
  input  x2,
  input  x1,
  input  x0,
  input  CP,
  input  CL,
  input  EN,
  output y7,
  output y6,
  output y5,
  output y4,
  output y3,
  output y2,
  output y1,
  output y0
);

  wire and_1_out, and_2_out, and_3_out, and_4_out, and_5_out, and_6_out, and_7_out, and_8_out, and_9_out,
       and_10_out, and_11_out, and_12_out, and_13_out, and_14_out, and_15_out, and_16_out, d_ff_1_q,
       d_ff_2_q, d_ff_3_q, d_ff_4_q, d_ff_5_q, d_ff_6_q, d_ff_7_q, d_ff_8_q, not_1_out, or_1_out, or_2_out,
       or_3_out, or_4_out, or_5_out, or_6_out, or_7_out, or_8_out;

  and and_1 (and_1_out, d_ff_1_q, not_1_out);
  or or_1 (or_1_out, and_1_out, and_2_out);
  and and_2 (and_2_out, x7, Load);
  D_Flip_Flop d_ff_1 (.clk(CP), .D(or_1_out), .Q(d_ff_1_q), .reset(CL));  // open: Qn, preset, en
  assign y7 = EN ? d_ff_1_q : 1'bz;  // Controlled_Buffer controlled_buffer_1
  and and_3 (and_3_out, d_ff_2_q, not_1_out);
  or or_2 (or_2_out, and_3_out, and_4_out);
  and and_4 (and_4_out, x6, Load);
  D_Flip_Flop d_ff_2 (.clk(CP), .D(or_2_out), .Q(d_ff_2_q), .reset(CL));  // open: Qn, preset, en
  assign y6 = EN ? d_ff_2_q : 1'bz;  // Controlled_Buffer controlled_buffer_2
  and and_5 (and_5_out, d_ff_3_q, not_1_out);
  and and_6 (and_6_out, x5, Load);
  or or_3 (or_3_out, and_5_out, and_6_out);
  D_Flip_Flop d_ff_3 (.clk(CP), .D(or_3_out), .Q(d_ff_3_q), .reset(CL));  // open: Qn, preset, en
  assign y5 = EN ? d_ff_3_q : 1'bz;  // Controlled_Buffer controlled_buffer_3
  and and_7 (and_7_out, d_ff_4_q, not_1_out);
  or or_4 (or_4_out, and_7_out, and_8_out);
  and and_8 (and_8_out, x4, Load);
  D_Flip_Flop d_ff_4 (.clk(CP), .D(or_4_out), .Q(d_ff_4_q), .reset(CL));  // open: Qn, preset, en
  assign y4 = EN ? d_ff_4_q : 1'bz;  // Controlled_Buffer controlled_buffer_4
  and and_9 (and_9_out, d_ff_5_q, not_1_out);
  and and_10 (and_10_out, x3, Load);
  or or_5 (or_5_out, and_9_out, and_10_out);
  D_Flip_Flop d_ff_5 (.clk(CP), .D(or_5_out), .Q(d_ff_5_q), .reset(CL));  // open: Qn, preset, en
  assign y3 = EN ? d_ff_5_q : 1'bz;  // Controlled_Buffer controlled_buffer_5
  and and_11 (and_11_out, d_ff_6_q, not_1_out);
  and and_12 (and_12_out, x2, Load);
  or or_6 (or_6_out, and_11_out, and_12_out);
  D_Flip_Flop d_ff_6 (.clk(CP), .D(or_6_out), .Q(d_ff_6_q), .reset(CL));  // open: Qn, preset, en
  assign y2 = EN ? d_ff_6_q : 1'bz;  // Controlled_Buffer controlled_buffer_6
  and and_13 (and_13_out, d_ff_7_q, not_1_out);
  or or_7 (or_7_out, and_13_out, and_14_out);
  and and_14 (and_14_out, x1, Load);
  D_Flip_Flop d_ff_7 (.clk(CP), .D(or_7_out), .Q(d_ff_7_q), .reset(CL));  // open: Qn, preset, en
  assign y1 = EN ? d_ff_7_q : 1'bz;  // Controlled_Buffer controlled_buffer_7
  and and_15 (and_15_out, d_ff_8_q, not_1_out);
  and and_16 (and_16_out, x0, Load);
  or or_8 (or_8_out, and_15_out, and_16_out);
  not not_1 (not_1_out, Load);
  D_Flip_Flop d_ff_8 (.clk(CP), .D(or_8_out), .Q(d_ff_8_q), .reset(CL));  // open: Qn, preset, en
  assign y0 = EN ? d_ff_8_q : 1'bz;  // Controlled_Buffer controlled_buffer_8

  // Notes on the sheet:
  //   1607091
endmodule

// 4 bit reg
module _4_bit_reg (
  input  Load,
  input  x3,
  input  x2,
  input  x1,
  input  x0,
  input  CLK,
  input  CL,
  input  EN,
  output y3,
  output y2,
  output y1,
  output y0
);

  wire and_1_out, and_2_out, and_3_out, and_4_out, and_5_out, and_6_out, and_7_out, and_8_out, d_ff_1_q,
       d_ff_2_q, d_ff_3_q, d_ff_4_q, not_1_out, or_1_out, or_2_out, or_3_out, or_4_out;

  and and_1 (and_1_out, d_ff_1_q, not_1_out);
  and and_2 (and_2_out, x3, Load);
  or or_1 (or_1_out, and_1_out, and_2_out);
  D_Flip_Flop d_ff_1 (.clk(CLK), .D(or_1_out), .Q(d_ff_1_q), .reset(CL));  // open: Qn, preset, en
  assign y3 = EN ? d_ff_1_q : 1'bz;  // Controlled_Buffer controlled_buffer_1
  and and_3 (and_3_out, d_ff_2_q, not_1_out);
  and and_4 (and_4_out, x2, Load);
  or or_2 (or_2_out, and_3_out, and_4_out);
  D_Flip_Flop d_ff_2 (.clk(CLK), .D(or_2_out), .Q(d_ff_2_q), .reset(CL));  // open: Qn, preset, en
  assign y2 = EN ? d_ff_2_q : 1'bz;  // Controlled_Buffer controlled_buffer_2
  and and_5 (and_5_out, d_ff_3_q, not_1_out);
  or or_3 (or_3_out, and_5_out, and_6_out);
  and and_6 (and_6_out, x1, Load);
  D_Flip_Flop d_ff_3 (.clk(CLK), .D(or_3_out), .Q(d_ff_3_q), .reset(CL));  // open: Qn, preset, en
  assign y1 = EN ? d_ff_3_q : 1'bz;  // Controlled_Buffer controlled_buffer_3
  and and_7 (and_7_out, d_ff_4_q, not_1_out);
  and and_8 (and_8_out, x0, Load);
  or or_4 (or_4_out, and_7_out, and_8_out);
  not not_1 (not_1_out, Load);
  D_Flip_Flop d_ff_4 (.clk(CLK), .D(or_4_out), .Q(d_ff_4_q), .reset(CL));  // open: Qn, preset, en
  assign y0 = EN ? d_ff_4_q : 1'bz;  // Controlled_Buffer controlled_buffer_4

  // Notes on the sheet:
  //   1607091
endmodule

module FA (
  input  A,
  input  B,
  input  Cin,
  output S,
  output Cout
);

  wire and_1_out, and_2_out, xor_1_out;

  xor xor_1 (xor_1_out, A, B);
  xor xor_2 (S, xor_1_out, Cin);
  and and_1 (and_1_out, Cin, xor_1_out);
  and and_2 (and_2_out, B, A);
  or or_1 (Cout, and_1_out, and_2_out);

  // Notes on the sheet:
  //   1607091
endmodule

module HA (
  input  A,
  input  B,
  output Sum,
  output Carry
);

  xor xor_1 (Sum, A, B);
  and and_1 (Carry, B, A);

  // Notes on the sheet:
  //   1607091
endmodule

// PC
module ProgramCounter (
  input  Cp,
  input  CLK,
  input  CLR,
  input  Ep,
  output [3:0] Output
);

  wire j_k_ff_1_q, j_k_ff_2_q, j_k_ff_3_q, j_k_ff_4_q, not_1_out, not_2_out, not_3_out, not_4_out;

  assign Output[3] = Ep ? j_k_ff_1_q : 1'bz;  // Controlled_Buffer controlled_buffer_1
  assign Output[2] = Ep ? j_k_ff_2_q : 1'bz;  // Controlled_Buffer controlled_buffer_2
  not not_1 (not_1_out, j_k_ff_2_q);
  J_K_Flip_Flop j_k_ff_1 (.J(Cp), .clk(not_1_out), .K(Cp), .Q(j_k_ff_1_q), .reset(CLR));  // open: Qn, preset, en
  assign Output[1] = Ep ? j_k_ff_3_q : 1'bz;  // Controlled_Buffer controlled_buffer_3
  not not_2 (not_2_out, j_k_ff_3_q);
  J_K_Flip_Flop j_k_ff_2 (.J(Cp), .clk(not_2_out), .K(Cp), .Q(j_k_ff_2_q), .reset(CLR));  // open: Qn, preset, en
  assign Output[0] = Ep ? j_k_ff_4_q : 1'bz;  // Controlled_Buffer controlled_buffer_4
  not not_3 (not_3_out, j_k_ff_4_q);
  J_K_Flip_Flop j_k_ff_3 (.J(Cp), .clk(not_3_out), .K(Cp), .Q(j_k_ff_3_q), .reset(CLR));  // open: Qn, preset, en
  J_K_Flip_Flop j_k_ff_4 (.J(Cp), .clk(not_4_out), .K(Cp), .Q(j_k_ff_4_q), .reset(CLR));  // open: Qn, preset, en
  not not_4 (not_4_out, CLK);

  // Notes on the sheet:
  //   1607091
endmodule

module IR (
  input  LOAD,
  input  CLK,
  input  [7:0] INPUT,
  input  ENABLE,
  input  CLR,
  output [3:0] OUTPUT0_3,
  output [3:0] OUTPUT4_7
);

  _4_bit_reg u_4_bit_reg_1 (
    .x3(INPUT[7]), .x2(INPUT[6]), .x1(INPUT[5]), .x0(INPUT[4]), .Load(LOAD), .CLK(CLK), .CL(CLR),
    .EN(ENABLE), .y3(OUTPUT4_7[3]), .y2(OUTPUT4_7[2]), .y1(OUTPUT4_7[1]), .y0(OUTPUT4_7[0]));
  _4_bit_reg u_4_bit_reg_2 (
    .x3(INPUT[3]), .x2(INPUT[2]), .x1(INPUT[1]), .x0(INPUT[0]), .Load(LOAD), .CLK(CLK), .CL(CLR),
    .EN(ENABLE), .y3(OUTPUT0_3[3]), .y2(OUTPUT0_3[2]), .y1(OUTPUT0_3[1]), .y0(OUTPUT0_3[0]));

  // Notes on the sheet:
  //   1607091
endmodule

// counter
module ringCounter (
  input  CLK,
  input  CLR,
  output T6,
  output T5,
  output T4,
  output T3,
  output T2,
  output T1
);

  wire j_k_ff_1_qn, j_k_ff_2_qn, j_k_ff_3_qn, j_k_ff_4_qn, j_k_ff_5_qn, j_k_ff_6_q, not_1_out;

  J_K_Flip_Flop j_k_ff_1 (
    .J(T5), .clk(not_1_out), .K(j_k_ff_2_qn), .Q(T6), .Qn(j_k_ff_1_qn), .reset(CLR));  // open: preset, en
  J_K_Flip_Flop j_k_ff_2 (
    .J(T4), .clk(not_1_out), .K(j_k_ff_3_qn), .Q(T5), .Qn(j_k_ff_2_qn), .reset(CLR));  // open: preset, en
  J_K_Flip_Flop j_k_ff_3 (
    .J(T3), .clk(not_1_out), .K(j_k_ff_4_qn), .Q(T4), .Qn(j_k_ff_3_qn), .reset(CLR));  // open: preset, en
  J_K_Flip_Flop j_k_ff_4 (
    .J(T2), .clk(not_1_out), .K(j_k_ff_5_qn), .Q(T3), .Qn(j_k_ff_4_qn), .reset(CLR));  // open: preset, en
  J_K_Flip_Flop j_k_ff_5 (
    .J(T1), .clk(not_1_out), .K(j_k_ff_6_q), .Q(T2), .Qn(j_k_ff_5_qn), .reset(CLR));  // open: preset, en
  J_K_Flip_Flop j_k_ff_6 (
    .J(j_k_ff_1_qn), .clk(not_1_out), .K(T6), .Q(j_k_ff_6_q), .Qn(T1), .reset(CLR));  // open: preset, en
  not not_1 (not_1_out, CLK);

  // Notes on the sheet:
  //   1607091
endmodule

// decoder
module Intruction_decoder (
  input  I7,
  input  I6,
  input  I5,
  input  I4,
  output LDA,
  output ADD,
  output SUB,
  output OUT,
  output HLT
);

  wire not_1_out, not_2_out, not_3_out, not_4_out;

  not not_1 (not_1_out, I7);
  not not_2 (not_2_out, I6);
  not not_3 (not_3_out, I5);
  not not_4 (not_4_out, I4);
  and and_1 (LDA, I7, not_2_out, I5, I4);
  and and_2 (ADD, not_1_out, I6, not_3_out, I4);
  and and_3 (SUB, not_1_out, I6, I5, I4);
  and and_4 (OUT, not_1_out, not_2_out, not_3_out, not_4_out);
  and and_5 (HLT, not_1_out, I6, not_3_out, not_4_out);

  // Notes on the sheet:
  //   1607091
endmodule

// Control
module ControlSequencer (
  input  [3:0] I7_I4,
  input  CLR,
  input  CLK,
  output HLT,
  output CP,
  output EP,
  output LMbar,
  output CEbar,
  output LIbar,
  output EIbar,
  output LAbar,
  output EA,
  output SU,
  output EU,
  output LBbar,
  output LObar
);

  wire and_1_out, and_2_out, and_3_out, and_4_out, and_5_out, and_6_out, and_7_out, and_8_out, and_9_out,
       and_10_out, and_11_out, and_12_out, and_15_out, and_16_out, and_17_out, and_18_out, decoder_1_add,
       decoder_1_lda, decoder_1_out, decoder_1_sub, or_1_out, or_2_out, or_3_out, or_4_out, or_6_out,
       ringcounter_1_t3, ringcounter_1_t4, ringcounter_1_t5, ringcounter_1_t6;

  Decoder decoder_1 (
    .I7(I7_I4[3]), .I6(I7_I4[2]), .I5(I7_I4[1]), .I4(I7_I4[0]), .LDA(decoder_1_lda), .ADD(decoder_1_add),
    .SUB(decoder_1_sub), .OUT(decoder_1_out), .HLT(HLT));
  and and_1 (and_1_out, decoder_1_add, ringcounter_1_t4);
  and and_2 (and_2_out, decoder_1_lda, ringcounter_1_t4);
  or or_1 (or_1_out, EP, and_2_out, and_1_out, and_3_out);
  not not_1 (LMbar, or_1_out);
  and and_3 (and_3_out, decoder_1_sub, ringcounter_1_t4);
  and and_4 (and_4_out, decoder_1_lda, ringcounter_1_t5);
  and and_5 (and_5_out, decoder_1_add, ringcounter_1_t5);
  or or_2 (or_2_out, ringcounter_1_t3, and_4_out, and_5_out, and_6_out);
  not not_2 (CEbar, or_2_out);
  and and_6 (and_6_out, decoder_1_sub, ringcounter_1_t5);
  not not_3 (LIbar, ringcounter_1_t3);
  and and_7 (and_7_out, decoder_1_lda, ringcounter_1_t4);
  and and_8 (and_8_out, decoder_1_add, ringcounter_1_t4);
  or or_3 (or_3_out, and_7_out, and_8_out, and_9_out);
  not not_4 (EIbar, or_3_out);
  ringCounter ringcounter_1 (
    .CLR(CLR), .T6(ringcounter_1_t6), .T5(ringcounter_1_t5), .T4(ringcounter_1_t4), .T3(ringcounter_1_t3),
    .T2(CP), .T1(EP), .CLK(CLK));
  and and_9 (and_9_out, decoder_1_sub, ringcounter_1_t4);
  and and_10 (and_10_out, decoder_1_lda, ringcounter_1_t5);
  and and_11 (and_11_out, decoder_1_add, ringcounter_1_t6);
  or or_4 (or_4_out, and_10_out, and_11_out, and_12_out);
  not not_5 (LAbar, or_4_out);
  and and_12 (and_12_out, decoder_1_sub, ringcounter_1_t6);
  and and_13 (EA, decoder_1_out, ringcounter_1_t4);
  and and_14 (SU, decoder_1_sub, ringcounter_1_t6);
  and and_15 (and_15_out, decoder_1_add, ringcounter_1_t6);
  and and_16 (and_16_out, decoder_1_sub, ringcounter_1_t6);
  or or_5 (EU, and_15_out, and_16_out);
  and and_17 (and_17_out, decoder_1_sub, ringcounter_1_t5);
  and and_18 (and_18_out, decoder_1_add, ringcounter_1_t5);
  or or_6 (or_6_out, and_18_out, and_17_out);
  not not_6 (LBbar, or_6_out);
  nand nand_1 (LObar, decoder_1_out, ringcounter_1_t4);

  // Notes on the sheet:
  //   HLT
  //   CP
  //   EP
  //   LMbar
  //   CEbar
  //   L1bar
  //   E1bar
  //   LAbar
  //   1607091
  //   SU
  //   EA
  //   EU
  //   LBbar
  //   LDA
  //   ADD
  //   SUB
  //   OUT
  //   LObar
endmodule

// Acc
module Accumulator (
  input  nLa,
  input  Clk,
  input  [7:0] \input ,
  output [7:0] Out
);

  wire not_1_out;

  _8_bit_reg u_8_bit_reg_1 (
    .x7(\input [7]), .x6(\input [6]), .x5(\input [5]), .x4(\input [4]), .x3(\input [3]), .x2(\input [2]),
    .x1(\input [1]), .x0(\input [0]), .Load(nLa), .CP(Clk), .CL(not_1_out), .EN(1'b1), .y7(Out[7]),
    .y6(Out[6]), .y5(Out[5]), .y4(Out[4]), .y3(Out[3]), .y2(Out[2]), .y1(Out[1]), .y0(Out[0]));
  not not_1 (not_1_out, 1'b1);

  // Notes on the sheet:
  //   1607091 and 1607115
  //   A Register
endmodule

// A S
module Adder_Subtractor (
  input  [7:0] A,
  input  [7:0] B,
  input  Cin,
  input  EU,
  output Cout,
  output [7:0] Out
);

  wire fa_1_cout, fa_2_cout, fa_3_cout, fa_4_cout, fa_5_cout, fa_6_cout, fa_7_cout;
  wire [7:0] fa_1_s;

  assign Out = EU ? fa_1_s : 8'bz;  // Controlled_Buffer controlled_buffer_1
  FA fa_1 (.A(A[0]), .B(B[0]), .Cin(Cin), .S(fa_1_s[0]), .Cout(fa_1_cout));
  FA fa_2 (.A(A[1]), .B(B[1]), .Cin(fa_1_cout), .S(fa_1_s[1]), .Cout(fa_2_cout));
  FA fa_3 (.A(A[2]), .B(B[2]), .Cin(fa_2_cout), .S(fa_1_s[2]), .Cout(fa_3_cout));
  FA fa_4 (.A(A[3]), .B(B[3]), .Cin(fa_3_cout), .S(fa_1_s[3]), .Cout(fa_4_cout));
  FA fa_5 (.A(A[4]), .B(B[4]), .Cin(fa_4_cout), .S(fa_1_s[4]), .Cout(fa_5_cout));
  FA fa_6 (.A(A[5]), .B(B[5]), .Cin(fa_5_cout), .S(fa_1_s[5]), .Cout(fa_6_cout));
  FA fa_7 (.A(A[6]), .B(B[6]), .Cin(fa_6_cout), .S(fa_1_s[6]), .Cout(fa_7_cout));
  FA fa_8 (.A(A[7]), .B(B[7]), .Cin(fa_7_cout), .S(fa_1_s[7]), .Cout(Cout));

  // Notes on the sheet:
  //   1607115
endmodule

// B reg
module B_register (
  input  nlb,
  input  Clk,
  input  [7:0] \input ,
  output [7:0] Out
);

  wire not_1_out;

  _8_bit_reg u_8_bit_reg_1 (
    .x7(\input [7]), .x6(\input [6]), .x5(\input [5]), .x4(\input [4]), .x3(\input [3]), .x2(\input [2]),
    .x1(\input [1]), .x0(\input [0]), .Load(nlb), .CP(Clk), .CL(not_1_out), .EN(1'b1), .y7(Out[7]),
    .y6(Out[6]), .y5(Out[5]), .y4(Out[4]), .y3(Out[3]), .y2(Out[2]), .y1(Out[1]), .y0(Out[0]));
  not not_1 (not_1_out, 1'b1);

  // Notes on the sheet:
  //   B Register
  //   1607115
endmodule

// Output
module output_register (
  input  nlo,
  input  Clk,
  input  [7:0] \input ,
  output [7:0] Out
);

  wire not_1_out;

  _8_bit_reg u_8_bit_reg_1 (
    .x7(\input [7]), .x6(\input [6]), .x5(\input [5]), .x4(\input [4]), .x3(\input [3]), .x2(\input [2]),
    .x1(\input [1]), .x0(\input [0]), .Load(nlo), .CP(Clk), .CL(not_1_out), .EN(1'b1), .y7(Out[7]),
    .y6(Out[6]), .y5(Out[5]), .y4(Out[4]), .y3(Out[3]), .y2(Out[2]), .y1(Out[1]), .y0(Out[0]));
  not not_1 (not_1_out, 1'b1);

  // Notes on the sheet:
  //   1607115
endmodule

module Decoder (
  input  I7,
  input  I6,
  input  I5,
  input  I4,
  output LDA,
  output ADD,
  output SUB,
  output OUT,
  output HLT
);

  wire and_1_out, and_2_out, and_3_out, and_4_out, not_1_out, not_2_out, not_3_out, not_4_out;

  not not_1 (not_1_out, I7);
  not not_2 (not_2_out, I6);
  not not_3 (not_3_out, I5);
  not not_4 (not_4_out, I4);
  and and_1 (and_1_out, not_1_out, not_2_out, not_3_out, not_4_out);
  and and_2 (and_2_out, not_1_out, not_2_out, not_3_out, I4);
  and and_3 (and_3_out, not_1_out, not_2_out, I5, not_4_out);
  and and_4 (and_4_out, I7, I6, I5, not_4_out);
  and and_5 (HLT, I7, I6, I5, I4);
  buf buffer_1 (LDA, and_1_out);
  buf buffer_2 (ADD, and_2_out);
  buf buffer_3 (SUB, and_3_out);
  buf buffer_4 (OUT, and_4_out);
endmodule

// Connector
module transfer (
  input  in_1,
  input  [7:0] from_B_reg,
  output [7:0] To_adder_subtractor
);

  xor xor_1 (To_adder_subtractor[7], in_1, from_B_reg[7]);
  xor xor_2 (To_adder_subtractor[5], in_1, from_B_reg[5]);
  xor xor_3 (To_adder_subtractor[6], in_1, from_B_reg[6]);
  xor xor_4 (To_adder_subtractor[4], in_1, from_B_reg[4]);
  xor xor_5 (To_adder_subtractor[3], in_1, from_B_reg[3]);
  xor xor_6 (To_adder_subtractor[2], in_1, from_B_reg[2]);
  xor xor_7 (To_adder_subtractor[1], in_1, from_B_reg[1]);
  xor xor_8 (To_adder_subtractor[0], in_1, from_B_reg[0]);

  // Notes on the sheet:
  //   1607091
endmodule
