// Logisim project main_project.circ as structural Verilog
module Adder_Subtractor (
  input  [7:0] A,
  input  [7:0] B,
  input  Add_Sub,
  output Cout,
  output [7:0] Output
);

  wire full_adder_2_cout, full_adder_3_cout, full_adder_4_cout, full_adder_5_cout, full_adder_6_cout,
       full_adder_7_cout, full_adder_8_cout, xor_1_out, xor_2_out, xor_3_out, xor_4_out, xor_5_out,
       xor_6_out, xor_7_out, xor_8_out;

  xor xor_1 (xor_1_out, B[7], Add_Sub);
  xor xor_2 (xor_2_out, B[6], Add_Sub);
  Full_Adder full_adder_1 (.A(A[7]), .B(xor_1_out), .Cin(full_adder_2_cout), .S(Output[7]), .Cout(Cout));
  xor xor_3 (xor_3_out, B[5], Add_Sub);
  Full_Adder full_adder_2 (.A(A[6]), .B(xor_2_out), .Cin(full_adder_3_cout), .S(Output[6]), .Cout(full_adder_2_cout));
  xor xor_4 (xor_4_out, B[4], Add_Sub);
  Full_Adder full_adder_3 (.A(A[5]), .B(xor_3_out), .Cin(full_adder_4_cout), .S(Output[5]), .Cout(full_adder_3_cout));
  xor xor_5 (xor_5_out, B[3], Add_Sub);
  Full_Adder full_adder_4 (.A(A[4]), .B(xor_4_out), .Cin(full_adder_5_cout), .S(Output[4]), .Cout(full_adder_4_cout));
  xor xor_6 (xor_6_out, B[2], Add_Sub);
  Full_Adder full_adder_5 (.A(A[3]), .B(xor_5_out), .Cin(full_adder_6_cout), .S(Output[3]), .Cout(full_adder_5_cout));
  xor xor_7 (xor_7_out, B[1], Add_Sub);
  Full_Adder full_adder_6 (.A(A[2]), .B(xor_6_out), .Cin(full_adder_7_cout), .S(Output[2]), .Cout(full_adder_6_cout));
  Full_Adder full_adder_7 (.A(A[1]), .B(xor_7_out), .Cin(full_adder_8_cout), .S(Output[1]), .Cout(full_adder_7_cout));
  xor xor_8 (xor_8_out, B[0], Add_Sub);
  Full_Adder full_adder_8 (.A(A[0]), .B(xor_8_out), .S(Output[0]), .Cout(full_adder_8_cout));  // open: Cin
endmodule

// FA
module Full_Adder (
  input  A,
  input  B,
  input  Cin,
  output S,
  output Cout
);

  wire and_1_out, and_2_out, xor_1_out;

  xor xor_1 (xor_1_out, A, B);
  and and_1 (and_1_out, A, B);
  xor xor_2 (S, xor_1_out, Cin);
  and and_2 (and_2_out, xor_1_out, Cin);
  or or_1 (Cout, and_2_out, and_1_out);
endmodule
